// Logisim project _main.circ as structural Verilog: 4 circuits, main circuit main
module main (
);

  wire and_1_out, button_1_out, clock_1_out, clock_2_out, DECODE_ENABLE, EXECUTE_ENABLE, FETCH_ENABLE,
       instruction_memory_1_p4, instruction_memory_1_p5, instruction_memory_1_p6,
       memory_controller_1_read_enable, memory_controller_1_write_enable, MEMORY_ENABLE,
       n6x8_register_file_1_p7, n6x8_register_file_1_p8, not_1_out, RAM_LOAD_ENABLE, RAM_STORE_ENABLE,
       register_read_logic_1_ra_enable, register_read_logic_1_rb_enable, rom_loader_1_ioenable,
       WRITEBACK_ENABLE;
  wire [2:0] counter_1_q;
  wire [3:0] instruction_memory_1_p2, instruction_memory_1_p3;
  wire [7:0] adder_1_out, instruction_memory_1_p7, n6x8_register_file_1_p3, n6x8_register_file_1_p4,
       RAM_ADDR, rom_loader_1_addrout, undriven, vala_valb_send_1_vala_out, vala_valb_send_1_vala_out_2;
  wire [23:0] RAM_DATA_IN, RAM_DATA_OUT, rom_loader_1_dataout;

  and and_1 (and_1_out, clock_1_out, not_1_out);
  Clock clock_1 (.out(clock_1_out));
  Button button_1 (.out(button_1_out));
  Counter #(.width(3), .max('h4)) counter_1 (.Q(counter_1_q), .clk(and_1_out));  // open: load, D, count, carry, clr
  Decoder #(.select(3), .disabled(0)) decoder_1 (
    .out0(FETCH_ENABLE), .out1(DECODE_ENABLE), .out2(EXECUTE_ENABLE), .out3(MEMORY_ENABLE),
    .out4(WRITEBACK_ENABLE), .sel(counter_1_q), .en(not_1_out));  // open: out5, out6, out7
  not not_1 (not_1_out, rom_loader_1_ioenable);
  ROM_loader rom_loader_1 (
    .RELOAD(button_1_out), .DATAOUT(rom_loader_1_dataout), .ADDROUT(rom_loader_1_addrout),
    .IOENABLE(rom_loader_1_ioenable));
  // Probe on RAM_ADDR
  // Probe on RAM_DATA_IN
  memory_controller memory_controller_1 (
    .read_enable(memory_controller_1_read_enable), .write_enable(memory_controller_1_write_enable),
    .icode(instruction_memory_1_p2));
  assign RAM_LOAD_ENABLE = FETCH_ENABLE ? memory_controller_1_read_enable : 1'bz;  // Controlled_Buffer controlled_buffer_1
  assign RAM_STORE_ENABLE = FETCH_ENABLE ? memory_controller_1_write_enable : 1'bz;  // Controlled_Buffer controlled_buffer_2
  assign RAM_ADDR = rom_loader_1_ioenable ? rom_loader_1_addrout : 8'bz;  // Controlled_Buffer controlled_buffer_3
  assign RAM_DATA_IN = rom_loader_1_ioenable ? rom_loader_1_dataout : 24'bz;  // Controlled_Buffer controlled_buffer_4
  // instruction_memory instruction_memory_1: pin names not known; wires that end beside it: FETCH_ENABLE, instruction_memory_1_p2, instruction_memory_1_p3, instruction_memory_1_p4, instruction_memory_1_p5, instruction_memory_1_p6, instruction_memory_1_p7
  Adder adder_1 (.a(instruction_memory_1_p7), .b(8'h1), .out(adder_1_out));  // open: cin, cout
  alu alu_1 (
    .ALU_A(undriven), .ALU_B(vala_valb_send_1_vala_out_2), .ALU_fun(instruction_memory_1_p3));  // open: FLAG, ALU_OUT
  // _6x8_Register_File 6x8_register_file_1: pin names not known; wires that end beside it: instruction_memory_1_p4, instruction_memory_1_p5, n6x8_register_file_1_p3, n6x8_register_file_1_p4, instruction_memory_1_p5, instruction_memory_1_p4, n6x8_register_file_1_p7, n6x8_register_file_1_p8
  and and_2 (n6x8_register_file_1_p7, register_read_logic_1_ra_enable, DECODE_ENABLE);
  and and_3 (n6x8_register_file_1_p8, register_read_logic_1_rb_enable, DECODE_ENABLE);
  Clock clock_2 (.out(clock_2_out));
  valA_valB_Send vala_valb_send_1 (
    .valA_in(n6x8_register_file_1_p3), .valA_in_2(n6x8_register_file_1_p4),
    .valA_out(vala_valb_send_1_vala_out), .valA_out_2(vala_valb_send_1_vala_out_2),
    .Enable_2({DECODE_ENABLE, 1'bz}));
  RAM #(.dataWidth(24), .bus("separate")) ram_1 (
    .addr(RAM_ADDR), .din(RAM_DATA_IN), .data(RAM_DATA_OUT), .str(RAM_STORE_ENABLE), .clk(clock_2_out),
    .ld(RAM_LOAD_ENABLE));  // open: sel, clr
  register_read_logic register_read_logic_1 (
    .rA_Enable(register_read_logic_1_ra_enable), .rB_Enable(register_read_logic_1_rb_enable),
    .icode(instruction_memory_1_p2));
endmodule

module instruction_memory (
  input  ENABLE,
  input  [7:0] NEWPC,
  output [3:0] ICODE,
  output [3:0] IFUN,
  output [3:0] rA,
  output [3:0] rB,
  output [7:0] valC,
  output [7:0] PC
);

  wire clock_1_out;
  wire [23:0] RAM_DATA_OUT;

  Register register_1 (.D(NEWPC), .en(ENABLE), .Q(PC), .clk(clock_1_out));  // open: clr
  Clock clock_1 (.out(clock_1_out));
  Register #(.width(24)) register_2 (
    .D(RAM_DATA_OUT), .en(ENABLE), .Q({valC, rB, rA, IFUN, ICODE}), .clk(clock_1_out));  // open: clr

  // Other names for the same wires on the sheet: RAM_ADDR[7:0] = PC; RAM_LOAD_ENABLE = ENABLE

  // Notes on the sheet:
  //   ENABLE: pull=down
endmodule

module register_read_logic (
  input  [3:0] icode,
  output rA_Enable,
  output rB_Enable
);

  wire and_1_out, and_2_out, and_3_out, and_4_out, and_5_out, and_6_out, and_7_out, not_1_out, not_2_out,
       not_3_out, not_4_out, not_5_out, not_6_out, not_7_out, not_8_out, not_9_out, not_10_out, not_11_out,
       not_13_out, not_14_out, not_15_out;

  not not_1 (not_1_out, icode[3]);
  not not_2 (not_2_out, icode[1]);
  not not_3 (not_3_out, icode[0]);
  not not_4 (not_4_out, icode[1]);
  not not_5 (not_5_out, icode[0]);
  not not_6 (not_6_out, icode[3]);
  not not_7 (not_7_out, icode[2]);
  not not_8 (not_8_out, icode[3]);
  and and_1 (and_1_out, not_8_out, not_9_out, not_10_out);
  not not_9 (not_9_out, icode[1]);
  not not_10 (not_10_out, icode[0]);
  not not_11 (not_11_out, icode[3]);
  not not_12 (not_11_out, icode[3]);
  and and_2 (and_2_out, not_11_out, icode[2], not_13_out);
  not not_13 (not_13_out, icode[1]);
  not not_14 (not_14_out, icode[3]);
  and and_3 (and_3_out, not_14_out, icode[2], not_15_out);
  not not_15 (not_15_out, icode[0]);
  and and_4 (and_4_out, not_1_out, not_2_out, not_3_out);
  and and_5 (and_5_out, icode[2], not_4_out, not_5_out);
  and and_6 (and_6_out, not_6_out, icode[2], icode[0]);
  and and_7 (and_7_out, icode[3], not_7_out, icode[1], icode[0]);
  or or_1 (rB_Enable, and_1_out, and_2_out, and_3_out);
  or or_2 (rA_Enable, and_4_out, and_5_out, and_6_out, and_7_out);
endmodule

module valA_valB_Send (
  input  [7:0] valA_in,
  input  [7:0] valA_in_2,
  input  Enable,
  input  Enable_2,
  output [7:0] valA_out,
  output [7:0] valA_out_2
);

  wire clock_1_out, undriven, undriven_2;

  Clock clock_1 (.out(clock_1_out));
  Register register_1 (.D(valA_in), .en(Enable), .Q(valA_out), .clk(clock_1_out), .clr(undriven));
  Register register_2 (.D(valA_in), .en(Enable), .Q(valA_out), .clk(clock_1_out), .clr(undriven));
  Register register_3 (.D(valA_in_2), .en(Enable), .Q(valA_out_2), .clk(clock_1_out), .clr(undriven_2));
  Register register_4 (.D(valA_in_2), .en(Enable), .Q(valA_out_2), .clk(clock_1_out), .clr(undriven_2));

  assign Enable_2 = Enable;
endmodule
