// Logisim project adder.circ as structural Verilog: 2 circuits, main circuit main
module main (
  input  in_1,
  input  [7:0] in_2,
  input  [7:0] in_3,
  output [7:0] out_4,
  output out_5
);

  Adder adder_1 (.a(in_2), .b(in_3), .out(out_4), .cin(in_1), .cout(out_5));
endmodule

module memory_control (
  input  in_1,
  input  [3:0] in_2,
  output out_3
);

  wire not_1_out;

  not not_1 (not_1_out, in_1);
  Multiplexer #(.select(4), .enable("false")) multiplexer_1 (
    .in0(in_1), .in1(in_1), .in2(in_1), .in3(in_1), .in4(not_1_out), .in5(in_1), .in6(in_1), .in7(in_1),
    .in8(in_1), .in9(in_1), .in10(in_1), .in11(in_1), .in12(not_1_out), .out(out_3), .sel(in_2));  // open: in13, in14, in15
endmodule
