// Logisim project alu.circ as structural Verilog: 1 circuit, main circuit main
module main (
);

  wire [7:0] adder_1_out, divider_1_out, multiplier_1_out, subtractor_1_out;

  Adder adder_1 (.out(adder_1_out));  // open: a, b, cin, cout
  Subtractor subtractor_1 (.out(subtractor_1_out));  // open: a, b, bin, bout
  Multiplier multiplier_1 (.out(multiplier_1_out));  // open: a, b, cin, cout
  Divider divider_1 (.out(divider_1_out));  // open: a, b, upper, rem
  Multiplexer #(.select(2), .width(8), .enable("false")) multiplexer_1 (
    .in0(adder_1_out), .in1(subtractor_1_out), .in2(multiplier_1_out), .in3(divider_1_out));  // open: out, sel
endmodule
