// Logisim project conditional_jump_logic.circ as structural Verilog: 1 circuit, main circuit ConditionJumpLogic
module ConditionJumpLogic (
  input  i0,
  input  i1,
  input  i2,
  input  i3,
  input  i4,
  output o0
);

  wire and_1_out, and_2_out, and_3_out, and_4_out, and_5_out, and_6_out, not_1_out, not_2_out, not_3_out,
       not_4_out, not_5_out, not_6_out, not_7_out, not_8_out, not_9_out, not_10_out, not_11_out, not_12_out;

  not not_1 (not_1_out, i0);
  not not_2 (not_2_out, i1);
  not not_3 (not_3_out, i3);
  not not_4 (not_4_out, i1);
  not not_5 (not_5_out, i2);
  not not_6 (not_6_out, i3);
  not not_7 (not_7_out, i2);
  not not_8 (not_8_out, i4);
  not not_9 (not_9_out, i0);
  not not_10 (not_10_out, i3);
  not not_11 (not_11_out, i4);
  not not_12 (not_12_out, i4);
  and and_1 (and_1_out, not_1_out, not_2_out, not_3_out);
  and and_2 (and_2_out, not_4_out, not_5_out, not_6_out, i4);
  and and_3 (and_3_out, not_7_out, i3, not_8_out);
  and and_4 (and_4_out, not_9_out, i2, not_10_out, not_11_out);
  and and_5 (and_5_out, i0, i3);
  and and_6 (and_6_out, i0, i1, not_12_out);
  or or_1 (o0, and_1_out, and_2_out, and_3_out, and_4_out, and_5_out, and_6_out);
endmodule
