// Logisim project memory_control.circ as structural Verilog: 1 circuit, main circuit memory_controller
module memory_controller (
  input  [3:0] icode,
  output read_enable,
  output write_enable
);

  wire and_1_out, and_2_out, and_3_out, and_4_out, and_5_out, and_6_out, not_1_out, not_2_out, not_3_out,
       not_4_out, not_5_out, not_6_out, not_7_out, not_8_out;

  not not_1 (not_1_out, icode[3]);
  not not_2 (not_2_out, icode[2]);
  not not_3 (not_3_out, icode[2]);
  not not_4 (not_4_out, icode[2]);
  not not_5 (not_5_out, icode[3]);
  not not_6 (not_6_out, icode[2]);
  not not_7 (not_7_out, icode[1]);
  not not_8 (not_8_out, icode[0]);
  and and_1 (and_1_out, not_1_out, not_2_out);
  and and_2 (and_2_out, not_3_out, icode[0]);
  and and_3 (and_3_out, not_4_out, icode[1]);
  and and_4 (and_4_out, icode[3], icode[2]);
  and and_5 (and_5_out, not_5_out, icode[2]);
  and and_6 (and_6_out, icode[3], not_6_out, not_7_out, not_8_out);
  or or_1 (read_enable, and_1_out, and_2_out, and_3_out, and_4_out);
  or or_2 (write_enable, and_5_out, and_6_out);
endmodule
