// Logisim project rom-ram.circ as structural Verilog: 1 circuit, main circuit main
module main (
);

  wire button_1_out, clock_1_out, controlled_buffer_2_out, counter_1_carry, not_1_out, not_2_out;
  wire [7:0] controlled_buffer_1_out, controlled_buffer_3_out, counter_1_q, rom_1_data;

  Counter counter_1 (
    .count(not_1_out), .Q(counter_1_q), .carry(counter_1_carry), .clk(clock_1_out), .clr(button_1_out));  // open: load, D
  not not_1 (not_1_out, counter_1_carry);
  Clock clock_1 (.out(clock_1_out));
  Button button_1 (.out(button_1_out));
  not not_2 (not_2_out, counter_1_carry);
  assign controlled_buffer_1_out = not_2_out ? counter_1_q : 8'bz;  // Controlled_Buffer controlled_buffer_1
  assign controlled_buffer_2_out = not_2_out ? not_2_out : 1'bz;  // Controlled_Buffer controlled_buffer_2
  assign controlled_buffer_3_out = not_2_out ? rom_1_data : 8'bz;  // Controlled_Buffer controlled_buffer_3
  ROM rom_1 (.addr(counter_1_q), .data(rom_1_data));  // open: sel
  RAM #(.bus("separate")) ram_1 (
    .addr(controlled_buffer_1_out), .din(controlled_buffer_3_out), .str(controlled_buffer_2_out),
    .clk(clock_1_out));  // open: data, sel, ld, clr

  // Notes on the sheet:
  //   contents of rom_1 (hex, n*v repeats v):
  //   256*11
endmodule
